# Fritzing sketch circuit (saved by Fritzing 0.9.2b)
circuit board: 8.46667cm x 5.64444cm
breadboards: 1

parts:
  Digispark1 = Digispark
  LED1 = LED - 5mm [color="White (6500K)" package="5 mm [THT]"]
  LED2 = LED - 5mm [color="White (6500K)" package="5 mm [THT]"]
  LED3 = LED - 5mm [color="White (6500K)" package="5 mm [THT]"]
  R1 = Resistor [tolerance=±5% resistance=100 package=THT]
  LED4 = LED - 5mm [color="White (6500K)" package="5 mm [THT]"]
  Alternate_switch = SPST Switch [package=switch-spdt_lock.007s]

nets:
  GND: Digispark1.GND, LED1.cathode, LED2.cathode, LED3.cathode, LED4.cathode, Alternate_switch.P
  N1: Digispark1.P0, Alternate_switch.S
  N2: Digispark1.P1, Digispark1.P2, R1.Pin_0
  N3: LED1.anode, LED2.anode, LED3.anode, R1.Pin_1, LED4.anode

custom parts:
  Digispark: The Digispark is an Attiny85 based microcontroller development board similar to the Arduino line, only cheaper, smaller, and a bit less powerful. With a whole host of shields to extend its functionality and the ability to use the familiar Arduino IDE the Digispark is a great way to jump into electronics, or perfect for when an Arduino is too big or too much.

// code stored in the sketch: prtScrnKey.ino
// Boards manager URL: http://digistump.com/package_digistump_index.json
// Board: Digispark (Default 16.5MHz)

#include <DigiKeyboard.h>

int ledPin = 1;
int buttonPin = 0;
int groundPin = 5;
int fade = 6;

int lastButtonState;
int buttonState;
int brighthess;

void notify() {
  for (int brightness = 40; brightness > 0; brightness -= fade) {
    analogWrite(ledPin, brightness);
    DigiKeyboard.delay(30);
  }
  analogWrite(ledPin, 0);
}

void sendKey(byte keyStroke, byte modifiers) {
  while (!usbInterruptIsReady()) {
    usbPoll();
    _delay_ms(5);
  }
  memset(DigiKeyboard.reportBuffer, 0, sizeof(DigiKeyboard.reportBuffer));
  DigiKeyboard.reportBuffer[0] = modifiers;
  DigiKeyboard.reportBuffer[1] = keyStroke;
  usbSetInterrupt(DigiKeyboard.reportBuffer, sizeof(DigiKeyboard.reportBuffer));
}

void setup() {
  pinMode(ledPin, OUTPUT);
  pinMode(buttonPin, INPUT);
  digitalWrite(buttonPin, HIGH); // PULLUP
  pinMode(groundPin, OUTPUT);
  digitalWrite(groundPin, LOW);
  notify(); // ready
  buttonState = digitalRead(buttonPin);
}

void loop() {
  // detect alternate switch altered
  for (lastButtonState = buttonState; lastButtonState == buttonState; buttonState = digitalRead(buttonPin)) {
    DigiKeyboard.delay(100);
  }
  digitalWrite(buttonPin, HIGH); // KEEP PULLUP

  // send Key Strokes; see http://www.usb.org/developers/hidpage/Hut1_12v2.pdf#page=53
  sendKey(0, 0); // all key up
  sendKey(70, MOD_ALT_LEFT);  // Alt + Tab (43) // PrtSc 70
  sendKey(0, MOD_ALT_LEFT);   // Alt
  sendKey(0, 0); // all key up
  notify();
}
